# Fritzing sketch Testing Computer (saved by Fritzing 0.9.3b)

parts:
  Part1 = Arduino Nano (Rev3.0)
  Part2 = HX711 Weighing Sensor Module
  Load_Cell1 = Load Cell - Red/white/black/green
  Transceiver1 = nRF24L01 [package=module]

nets:
  GND: Part1.GND, Part2.GND, Transceiver1.GND
  N1: Part1.D2, Part2.CK/TX
  N2: Part1.D3, Part2.DO/RX
  N3: Part1.D9, Transceiver1.CE
  N4: Part1.D10, Transceiver1.CSN
  N5: Part1.D11/MOSI, Transceiver1.MOSI
  N6: Part1.D12/MISO, Transceiver1.MISO
  VIN: Part1.VIN, Part2.VCC
  3V3: Part1.3V3, Transceiver1.VCC
  N7: Part1.D13/SCK, Transceiver1.SCK
  N8: Part2.E+, Load_Cell1.wire1
  N9: Part2.E-, Load_Cell1.wire3
  N10: Part2.A+, Load_Cell1.wire4
  N11: Part2.A-, Load_Cell1.wire2

custom parts:
  Load Cell - Red/white/black/green: A rectangle load cell/weighting pressure Sensor with four wires - Red, white, black, green. Normally corresponding with E+, E-, A+, A- respectively.
  nRF24L01: nRF24L01 module
