# Fritzing sketch Schematic (saved by Fritzing 0.9.3b)
circuit board: 10cm x 10cm
breadboards: 1

parts:
  Part1 = Arduino Nano (Rev3.0) (ICSP)
  BAT1 = BC9VPC [package=bc9vpc]
  M1 = BMP280
  Part2 = InvenSense MPU6050
  microSD1 = MicroSD Card Module

nets:
  N1: Part1.D10, microSD1.CS
  N2: Part1.D11/MOSI, microSD1.MOSI
  N3: Part1.D12/MISO, microSD1.MISO
  VIN: Part1.VIN, BAT1.V+, M1.VIN, Part2.VCC, microSD1.VCC
  GND: Part1.GND, BAT1.V-, M1.GND, Part2.GND, microSD1.GND
  N4: Part1.A5, M1.SCL, Part2.SCL
  N5: Part1.A4, M1.SDA, Part2.SDA
  N6: Part1.D13/SCK, microSD1.SCK

custom parts:
  BMP280: Temperature Humidity Barometric presure Sensor, I2C
